// Logisim project TallerLogica-Combinatorios.circ as structural Verilog: 13 circuits, main circuit verificador
module sumador_simple (
  input  A,
  input  B,
  output S,
  output Cout
);

  xor xor_1 (S, A, B);
  and and_1 (Cout, B, A);
endmodule

module sumador_completo (
  input  Cin,
  input  A,
  input  B,
  output S,
  output Cout
);

  wire sumador_simple_1_cout, sumador_simple_2_cout, sumador_simple_2_s;

  sumador_simple sumador_simple_1 (.A(Cin), .B(sumador_simple_2_s), .S(S), .Cout(sumador_simple_1_cout));
  sumador_simple sumador_simple_2 (.A(A), .B(B), .S(sumador_simple_2_s), .Cout(sumador_simple_2_cout));
  or or_1 (Cout, sumador_simple_1_cout, sumador_simple_2_cout);
endmodule

module sumador_4 (
  input  Cin,
  input  [3:0] A,
  input  [3:0] B,
  output [3:0] S,
  output Cout
);

  wire sumador_completo_1_cout, sumador_completo_2_cout, sumador_completo_3_cout;

  sumador_completo sumador_completo_1 (.Cin(Cin), .A(A[0]), .B(B[0]), .S(S[0]), .Cout(sumador_completo_1_cout));
  sumador_completo sumador_completo_2 (
    .Cin(sumador_completo_1_cout), .A(A[1]), .B(B[1]), .S(S[1]), .Cout(sumador_completo_2_cout));
  sumador_completo sumador_completo_3 (
    .Cin(sumador_completo_2_cout), .A(A[2]), .B(B[2]), .S(S[2]), .Cout(sumador_completo_3_cout));
  sumador_completo sumador_completo_4 (.Cin(sumador_completo_3_cout), .A(A[3]), .B(B[3]), .S(S[3]), .Cout(Cout));
  Hex_Digit_Display hex_digit_display_1 (.value(S));  // open: dp
endmodule

module comparador_cero (
  input  [3:0] A,
  output Z
);

  wire or_1_out, or_2_out, or_3_out;

  or or_1 (or_1_out, A[0], A[1]);
  or or_2 (or_2_out, A[2], A[3]);
  or or_3 (or_3_out, or_1_out, or_2_out);
  not not_1 (Z, or_3_out);
endmodule

module sumador_flags (
  input  Cin,
  input  [3:0] A,
  input  [3:0] B,
  output [3:0] S,
  output N,
  output Z,
  output V,
  output C
);

  wire and_1_out, and_2_out, not_1_out, not_2_out, not_3_out;

  not not_1 (not_1_out, B[3]);
  not not_2 (not_2_out, A[3]);
  not not_3 (not_3_out, N);
  sumador_4 sumador_4_1 (.Cin(Cin), .A(A), .B(B), .S({N, S[2:0]}), .Cout(C));
  and and_1 (and_1_out, not_1_out, N, not_2_out);
  and and_2 (and_2_out, A[3], not_3_out, B[3]);
  Hex_Digit_Display hex_digit_display_1 (.value({N, S[2:0]}));  // open: dp
  or or_1 (V, and_1_out, and_2_out);
  comparador_cero comparador_cero_1 (.A({N, S[2:0]}), .Z(Z));

  assign S[3] = N;
endmodule

module incrementador_4 (
  input  [3:0] A,
  output [3:0] S
);

  wire sumador_simple_1_cout, sumador_simple_2_cout, sumador_simple_3_cout;

  sumador_simple sumador_simple_1 (.A(A[0]), .B(1'b1), .S(S[0]), .Cout(sumador_simple_1_cout));
  sumador_simple sumador_simple_2 (.A(sumador_simple_1_cout), .B(A[1]), .S(S[1]), .Cout(sumador_simple_2_cout));
  sumador_simple sumador_simple_3 (.A(sumador_simple_2_cout), .B(A[2]), .S(S[2]), .Cout(sumador_simple_3_cout));
  sumador_simple sumador_simple_4 (.A(sumador_simple_3_cout), .B(A[3]), .S(S[3]));  // open: Cout
  Hex_Digit_Display hex_digit_display_1 (.value(S));  // open: dp
endmodule

module inversor_4 (
  input  [3:0] A,
  input  INV,
  output [3:0] S
);

  wire [3:0] incrementador_4_1_s, not_1_out;

  assign not_1_out = ~A;  // NOT_Gate not_1, 4 bits wide
  incrementador_4 incrementador_4_1 (.A(not_1_out), .S(incrementador_4_1_s));
  Hex_Digit_Display hex_digit_display_1 (.value(S));  // open: dp
  Multiplexer #(.width(4)) multiplexer_1 (.in0(A), .in1(incrementador_4_1_s), .out(S), .sel(INV));
endmodule

module ALU (
  input  [3:0] A,
  input  [3:0] B,
  input  [1:0] OP,
  output N,
  output Z,
  output V,
  output C,
  output [3:0] S
);

  wire [3:0] and_1_out, or_1_out, resta_flags_1_n, resta_flags_1_s, sumador_flags_1_n, sumador_flags_1_s;
  wire [3:1] comparador_cero_1_z, comparador_cero_2_z;

  sumador_flags sumador_flags_1 (
    .A(A), .B(B), .S(sumador_flags_1_s), .N(sumador_flags_1_n[0]), .Z(sumador_flags_1_n[1]),
    .V(sumador_flags_1_n[2]), .C(sumador_flags_1_n[3]));  // open: Cin
  and and_1 (and_1_out[0], B[0], A[0]);
  and and_2 (and_1_out[1], B[1], A[1]);
  and and_3 (and_1_out[2], B[2], A[2]);
  and and_4 (and_1_out[3], B[3], A[3]);
  or or_1 (or_1_out[0], B[0], A[0]);
  or or_2 (or_1_out[1], B[1], A[1]);
  or or_3 (or_1_out[2], B[2], A[2]);
  or or_4 (or_1_out[3], B[3], A[3]);
  comparador_cero comparador_cero_1 (.A(and_1_out), .Z(comparador_cero_1_z[1]));
  not not_1 (comparador_cero_1_z[3], 1'b1);
  resta_flags resta_flags_1 (
    .A(A), .B(B), .S(resta_flags_1_s), .N(resta_flags_1_n[0]), .Z(resta_flags_1_n[1]),
    .V(resta_flags_1_n[2]), .C(resta_flags_1_n[3]));  // open: Cin
  not not_2 (comparador_cero_1_z[2], 1'b1);
  comparador_cero comparador_cero_2 (.A(or_1_out), .Z(comparador_cero_2_z[1]));
  Multiplexer #(.select(2), .width(4)) multiplexer_1 (
    .in0(sumador_flags_1_s), .in1(resta_flags_1_s), .in2(and_1_out), .in3(or_1_out), .out(S), .sel(OP));
  not not_3 (comparador_cero_2_z[3], 1'b1);
  not not_4 (comparador_cero_2_z[2], 1'b1);
  Multiplexer #(.select(2), .width(4)) multiplexer_2 (
    .in0(sumador_flags_1_n), .in1(resta_flags_1_n), .in2({comparador_cero_1_z, and_1_out[3]}),
    .in3({comparador_cero_2_z, or_1_out[3]}), .out({C, V, Z, N}), .sel(OP));
  Hex_Digit_Display hex_digit_display_1 (.value(S));  // open: dp
endmodule

module verificador (
  output [3:0] out_1,
  output [3:0] out_2,
  output [1:0] out_3,
  output halt,
  output N,
  output Z,
  output V,
  output C,
  output [3:0] res
);

  wire clock_1_out;

  Clock clock_1 (.out(clock_1_out));
  Counter #(.max('h3ff), .width(10)) counter_1 (
    .clk(clock_1_out), .carry(halt), .Q({out_3, out_2, out_1}));  // open: clr, load, up, count, D
  ALU alu_1 (.A(out_1), .B(out_2), .OP(out_3), .N(N), .Z(Z), .V(V), .C(C), .S(res));
endmodule

module resta_simple (
  input  A,
  input  B,
  output R,
  output Borrow
);

  wire not_1_out;

  not not_1 (not_1_out, A);
  xor xor_1 (R, A, B);
  and and_1 (Borrow, B, not_1_out);
endmodule

module resta_completo (
  input  Cin,
  input  A,
  input  B,
  output R,
  output Borrow
);

  wire resta_simple_1_borrow, resta_simple_2_borrow, resta_simple_2_r;

  resta_simple resta_simple_1 (.A(resta_simple_2_r), .B(Cin), .R(R), .Borrow(resta_simple_1_borrow));
  resta_simple resta_simple_2 (.A(A), .B(B), .R(resta_simple_2_r), .Borrow(resta_simple_2_borrow));
  or or_1 (Borrow, resta_simple_1_borrow, resta_simple_2_borrow);
endmodule

module resta_4 (
  input  Cin,
  input  [3:0] A,
  input  [3:0] B,
  output [3:0] R,
  output Borrow
);

  wire resta_completo_1_borrow, resta_completo_2_borrow, resta_completo_3_borrow;

  resta_completo resta_completo_1 (.Cin(Cin), .A(A[0]), .B(B[0]), .R(R[0]), .Borrow(resta_completo_1_borrow));
  resta_completo resta_completo_2 (
    .Cin(resta_completo_1_borrow), .A(A[1]), .B(B[1]), .R(R[1]), .Borrow(resta_completo_2_borrow));
  resta_completo resta_completo_3 (
    .Cin(resta_completo_2_borrow), .A(A[2]), .B(B[2]), .R(R[2]), .Borrow(resta_completo_3_borrow));
  resta_completo resta_completo_4 (.Cin(resta_completo_3_borrow), .A(A[3]), .B(B[3]), .R(R[3]), .Borrow(Borrow));
  Hex_Digit_Display hex_digit_display_1 (.value(R));  // open: dp
endmodule

module resta_flags (
  input  Cin,
  input  [3:0] A,
  input  [3:0] B,
  output [3:0] S,
  output N,
  output Z,
  output V,
  output C
);

  wire and_1_out, and_2_out, not_1_out, not_2_out, not_3_out;

  resta_4 resta_4_1 (.Cin(Cin), .A(A), .B(B), .R({N, S[2:0]}), .Borrow(C));
  not not_1 (not_1_out, A[3]);
  not not_2 (not_2_out, B[3]);
  not not_3 (not_3_out, N);
  and and_1 (and_1_out, not_1_out, N, B[3]);
  and and_2 (and_2_out, A[3], not_2_out, not_3_out);
  Hex_Digit_Display hex_digit_display_1 (.value({N, S[2:0]}));  // open: dp
  comparador_cero comparador_cero_1 (.A({N, S[2:0]}), .Z(Z));
  or or_1 (V, and_1_out, and_2_out);

  assign S[3] = N;
endmodule
